# Fritzing sketch liverwort_incubator_v2 (saved by Fritzing 0.9.2b)
breadboards: 1

parts:
  Part1 = Adafruit PCF8523 RTC [part_number="Adafruit #3295"]
  Part2 = Adafruit Metro Mini [part_number="Adafruit #2590"]
  Q1 = Basic FET N-Channel [package="TO220 [THT]"]
  Part4 = Adafruit SHT31-D Sensirion Temperature/Humidity Sensor [part_number="Adafruit #2857"]
  Part5 = Adafruit TSL2561 [part_number="Adafruit #439"]
  Outside_fan_#2 = Header 4 [package=screwterminal-3.5mm-4_lock]
  Outside_fan_#1 = Header 4 [package=screwterminal-3.5mm-4_lock]
  Inside_fan_#2 = Header 4 [package=screwterminal-3.5mm-4_lock]
  Inside_fan_#1 = Header 4 [package=screwterminal-3.5mm-4_lock]
  peltier_#2 = Peltier Element
  peltier_#1 = Peltier Element
  12V_strip_of_white_LED_#4 = LEDs [package=led-1206]
  12V_strip_of_white_LED_#5 = LEDs [package=led-1206]
  12V_strip_of_white_LED_#6 = LEDs [package=led-1206]
  Switching_12V_power_supply1 = Power plug
  J4 = longpad pin header, 2 pins [form="long pad"]
  J7 = longpad pin header, 2 pins [form="long pad"]
  J8 = female pin header, 2 pins [form="♀ (female)"]
  J9 = female pin header, 2 pins [form="♀ (female)"]
  J6 = longpad pin header, 2 pins [form="long pad"]
  Q3 = Basic FET N-Channel [package="TO220 [THT]"]
  R1 = Resistor [tolerance=±5% resistance=10k package="2010 [SMD]"]
  R2 = Resistor [tolerance=±5% resistance=10k package="2010 [SMD]"]
  Part3 = Adafruit MicroSD card breakout board [part_number="Adafruit #254"]
  D1 = Diode [package=diode-1n4001]  # not connected
  Switching_5V_power_supply = Power plug
  U1 = 2-Channel 5v Relay Shield [package=relay-2ch5v10a]
  S1 = Toggle Switch [package=THT]

nets:
  VCC: Part1.VCC, Part2.+5V, Part4.VIN, Part5.VIN, J9.pin1, Part3.VCC, Switching_5V_power_supply.VCC, U1.VCC
  GND: Part1.GND, Q1.source, Outside_fan_#2.1, Outside_fan_#1.1, Switching_12V_power_supply1.GND, J6.pin1, Q3.source, R1.Pin_0, R2.Pin_0, Part3.GND, Switching_5V_power_supply.GND, U1.GND, S1.COM
  N1: Part2.AD5/SCL, Part4.SCL, Part5.SCL, J7.pin2
  N2: Part2.AD4/SDA, Part4.SDA, Part5.SDA, J7.pin1
  N3: Part2.IO13, Part3.CLK
  N4: Part2.IO12, Part3.DO
  N5: Part2.IO11, Part3.DI
  N6: Part2.IO10, Part2.IO9, Part3.CS, Part3.CD
  N7: Part2.IO7, U1.IN2
  N8: Part2.IO6, U1.IN1
  N9: Part2.IO5, Q1.gate, R1.Pin_1
  N10: Part2.IO4, Q3.gate, R2.Pin_1
  N11: Part2.IO3, Outside_fan_#2.4, Outside_fan_#1.4, Inside_fan_#2.4, Inside_fan_#1.4, J8.pin1
  3.3V: Part2.3.3V, Part3.+3V3
  N12: Q1.drain, 12V_strip_of_white_LED_#5.C, 12V_strip_of_white_LED_#6.A
  GND_2: Part4.GND, Part5.GND, Inside_fan_#2.1, Inside_fan_#1.1, J4.pin1
  N13: Outside_fan_#2.2, Outside_fan_#1.2, Inside_fan_#2.2, Inside_fan_#1.2, 12V_strip_of_white_LED_#6.C, Switching_12V_power_supply1.VCC, J4.pin2, J6.pin2, U1.K2-In
  N14: peltier_#2.pin1, peltier_#1.pin1, U1.K1-Off, U1.K2-On
  N15: peltier_#2.pin2, peltier_#1.pin2, U1.K1-On, U1.K2-Off
  N16: 12V_strip_of_white_LED_#4.C, 12V_strip_of_white_LED_#5.A
  N17: Q3.drain, U1.K1-In

custom parts:
  Adafruit PCF8523 RTC: This is a great battery-backed real time clock (RTC) that allows your microcontroller project to keep track of time even if it is reprogrammed, or if the power is lost. Perfect for datalogging, clock-building, time stamping, timers and alarms, etc. Equipped with PCF8523 RTC - it can run from 3.3V or 5V power & logic! Works great with an Arduino using our RTC library, with CircuitPython or with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
  Adafruit Metro Mini: We sure love the ATmega328 here at Adafruit, and we use them a lot for our own projects. The processor has plenty of GPIO, Analog inputs, hardware UART SPI and I2C, timers and PWM galore - just enough for most simple projects. When we need to go small, we use a Pro Trinket 3V or 5V, but if you want to have USB-to-Serial built in, we reach for an Adafruit METRO Mini. METRO Mini is the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
  Adafruit SHT31-D Sensirion Temperature/Humidity Sensor: Sensirion Temperature/Humidity sensors are some of the finest & highest-accuracy devices you can get. And, finally we have some that have a true I2C interface for easy reading. The SHT31-D sensor has an excellent ±2% relative humidity and ±0.3°C accuracy for most uses. Unlike earlier SHT sensors, this sensor has a true I2C interface, and (bonus!) even with two address options. It also is 3V or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
  Adafruit TSL2561: The TSL2561 luminosity sensor is an advanced digital light sensor, ideal for use in a wide range of light situations. Compared to low cost CdS cells, this sensor is more precise, allowing for exact lux calculations and can be configured for different gain/timing ranges to detect light ranges from up to 0.1 - 40,000+ Lux on the fly. The best part of this sensor is that it contains both infrared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
  Adafruit MicroSD card breakout board: Not just a simple breakout board, this microSD adapter goes the extra mile - designed for ease of use. Onboard 5v->3v regulator provides 150mA for power-hungry cards 3v level shifting means you can use this with ease on either 3v or 5v systems Uses a proper level shifting chip, not resistors: less problems, and faster read/write access Use 3 or 4 digital pins to read and write 2Gb+ of storage!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
  2-Channel 5v Relay Shield: 2 Channel 5v Relay Shield w. 2x SPD-06VDC-SD-C
